// Logisim project lab2.circ as structural Verilog: 1 circuit, main circuit main
module main (
  input  in_1,
  input  in_2,
  input  in_3,
  input  in_4,
  input  in_5,
  input  in_6,
  input  in_7,
  input  in_8,
  input  in_9,
  input  in_10,
  input  in_11,
  input  in_12,
  output out_13,
  output out_14,
  output out_15,
  output out_16
);

  wire and_1_out, and_2_out, and_3_out, and_4_out, and_5_out, and_7_out, and_8_out, and_9_out, or_1_out,
       or_2_out, or_3_out, or_5_out, or_6_out, or_7_out, or_8_out, or_9_out;

  and and_1 (and_1_out, ~in_2, ~in_4, in_6);  // AND_Gate
  and and_2 (and_2_out, ~in_2, in_4, in_6);  // AND_Gate
  and and_3 (and_3_out, in_2, ~in_4, ~in_6);  // AND_Gate
  and and_4 (and_4_out, ~in_2, in_4, ~in_6);  // AND_Gate
  and and_5 (and_5_out, in_2, in_4, ~in_6);  // AND_Gate
  or or_1 (or_1_out, in_9, in_11, in_12);
  or or_2 (or_2_out, ~in_9, ~in_11, ~in_12);  // OR_Gate
  or or_3 (or_3_out, in_9, ~in_11, in_12);  // OR_Gate
  or or_4 (out_14, and_1_out, and_2_out, and_3_out, and_4_out, and_5_out);
  and and_6 (out_16, or_1_out, or_3_out, or_2_out);
  and and_7 (and_7_out, ~in_1, ~in_3, ~in_5);  // AND_Gate
  and and_8 (and_8_out, in_1, in_5);  // AND_Gate
  and and_9 (and_9_out, in_1, in_3, in_5);
  or or_5 (or_5_out, in_7, in_8, ~in_10);  // OR_Gate
  or or_6 (or_6_out, in_7, ~in_8, in_10);  // OR_Gate
  or or_7 (or_7_out, in_7, ~in_8, ~in_10);  // OR_Gate
  or or_8 (or_8_out, ~in_7, in_8, in_10);  // OR_Gate
  or or_9 (or_9_out, ~in_7, ~in_8, in_10);  // OR_Gate
  or or_10 (out_13, and_7_out, and_8_out, and_9_out);
  and and_10 (out_15, or_5_out, or_6_out, or_7_out, or_8_out, or_9_out);

  // Notes on the sheet:
  //   Circut 1
  //   Kevin Yin
  //   Circut 2
endmodule
